// Logisim project Fibonacci.circ as structural Verilog: 1 circuit, main circuit main
module main (
);

  wire button_1_out, button_2_out, d_ff_1_qn;
  wire [7:0] adder_1_out, multiplexer_1_out, register_1_q, register_2_q;

  D_Flip_Flop d_ff_1 (.D(1'b1), .clk(button_1_out), .Qn(d_ff_1_qn), .reset(button_2_out));  // open: Q, preset
  Button button_1 (.out(button_1_out));
  Button button_2 (.out(button_2_out));
  Register register_1 (.D(multiplexer_1_out), .en(1'b1), .clk(button_1_out), .Q(register_1_q), .clr(button_2_out));
  Multiplexer #(.width(8)) multiplexer_1 (.in0(adder_1_out), .in1(8'h1), .out(multiplexer_1_out), .sel(d_ff_1_qn));
  Register register_2 (.D(register_1_q), .en(1'b1), .clk(button_1_out), .Q(register_2_q), .clr(button_2_out));
  Adder adder_1 (.a(register_1_q), .b(register_2_q), .out(adder_1_out));  // open: cin, cout
  Hex_Digit_Display hex_digit_display_1 (.value(adder_1_out[7:4]));  // open: dp
  Hex_Digit_Display hex_digit_display_2 (.value(adder_1_out[3:0]));  // open: dp
endmodule
