// Logisim project Clock_divider.circ as structural Verilog: 1 circuit, main circuit main
module main (
);

  wire Clock_out, d_ff_1_q, not_1_out;

  Button Clock (.out(Clock_out));
  LED led_1 (.in(Clock_out));
  not not_1 (not_1_out, d_ff_1_q);
  D_Flip_Flop d_ff_1 (.D(not_1_out), .clk(Clock_out), .Q(d_ff_1_q));  // open: Qn, preset, reset
  LED led_2 (.in(d_ff_1_q));

  // Notes on the sheet:
  //   Output
endmodule
