// Logisim project Fibonacci.circ as structural Verilog: 1 circuit, main circuit main
module main (
);

  wire Clock_out, d_ff_1_qn, Reset_out;
  wire [7:0] adder_1_out, multiplexer_1_out, register_1_q, register_2_q;

  Button Clock (.out(Clock_out));
  Button Reset (.out(Reset_out));
  Adder adder_1 (.a(register_1_q), .b(register_2_q), .out(adder_1_out));  // open: cin, cout
  D_Flip_Flop d_ff_1 (.D(1'b1), .clk(Clock_out), .Qn(d_ff_1_qn), .reset(Reset_out));  // open: Q, preset
  Multiplexer #(.width(8)) multiplexer_1 (.in0(adder_1_out), .in1(8'h1), .out(multiplexer_1_out), .sel(d_ff_1_qn));
  Register register_1 (.D(multiplexer_1_out), .en(1'b1), .clk(Clock_out), .Q(register_1_q), .clr(Reset_out));
  Register register_2 (.D(register_1_q), .en(1'b1), .clk(Clock_out), .Q(register_2_q), .clr(Reset_out));
  Hex_Digit_Display hex_digit_display_1 (.value(register_2_q[7:4]));  // open: dp
  Hex_Digit_Display hex_digit_display_2 (.value(register_2_q[3:0]));  // open: dp

  // Notes on the sheet:
  //   8 bit adder
  //   A+B
  //   Initialization FF
  //   Register A
  //   Register B
  //   Output
endmodule
