// Logisim project Sync_counter.circ as structural Verilog: 1 circuit, main circuit main
module main (
);

  wire button_1_out;
  wire [7:0] adder_1_out, register_1_q;

  Adder adder_1 (.a(register_1_q), .b(8'h1), .out(adder_1_out));  // open: cin, cout
  Button button_1 (.out(button_1_out));
  Register register_1 (.D(adder_1_out), .clk(button_1_out), .Q(register_1_q));  // open: en, clr
endmodule
