// Logisim project traffic.circ as structural Verilog: 1 circuit, main circuit main
module main (
);

  wire clock_1_out;
  wire [3:0] register_1_q;
  wire [7:0] rom_1_data;
  wire [7:4] register_1_q_2;
  wire [7:7] button_1_out;

  Button button_1 (.out(button_1_out[7]));
  ROM rom_1 (.addr({button_1_out[7], 3'b000, register_1_q}), .data(rom_1_data));
  Clock clock_1 (.out(clock_1_out));
  Register register_1 (.D(rom_1_data), .clk(clock_1_out), .Q({register_1_q_2, register_1_q}));  // open: en, clr
  LED led_1 (.in(register_1_q_2[4]));
  LED led_2 (.in(register_1_q_2[5]));
  LED led_3 (.in(register_1_q_2[6]));
  LED led_4 (.in(register_1_q_2[7]));

  // Notes on the sheet:
  //   contents of rom_1 (hex, n*v repeats v):
  //   41 22 10
  //   x10
  //   x20
  //   x40
  //   x80
endmodule
