// Logisim project urisc.circ as structural Verilog: 1 circuit, main circuit URISC_evo
module URISC_evo (
);

  wire and_1_out, clock_1_out, comparator_1_eq, comparator_1_gt, comparator_1_lt, decoder_1_out1,
       decoder_1_out2, decoder_1_out3, decoder_1_out4, multiplexer_1_out, not_1_out, not_2_out;
  wire [2:0] ROM_1_data, ROM_1_data_2, ROM_1_data_4;
  wire [7:0] Prefix_AND_out, Prefix_q;
  wire [7:3] ROM_1_data_5;
  wire [7:7] decoder_1_out0;
  wire [15:0] adder_1_out, DM_dout, multiplexer_2_out, multiplexer_3_out, PC_q, REG_B_q, REG_P_q,
       subtractor_1_out;
  wire [15:11] ROM_1_data_3;

  Clock clock_1 (.out(clock_1_out));
  and and_1 (and_1_out, multiplexer_1_out, decoder_1_out1);
  Decoder #(.select(3)) decoder_1 (
    .out0(decoder_1_out0[7]), .out1(decoder_1_out1), .out2(decoder_1_out2), .out3(decoder_1_out3),
    .out4(decoder_1_out4), .sel(ROM_1_data_2));  // open: out5, out6, out7, en
  Multiplexer #(.select(3), .enable("false")) multiplexer_1 (
    .in0(1'b1), .in1(comparator_1_gt), .in2(comparator_1_eq), .in3(comparator_1_lt), .in4(not_1_out),
    .out(multiplexer_1_out), .sel(ROM_1_data));  // open: in5, in6, in7
  Counter #(.width(16), .max('hffff)) PC (
    .load(and_1_out), .clk(clock_1_out), .D(multiplexer_3_out), .Q(PC_q));  // open: clr, up, count, carry
  Register #(.width(16)) REG_P (
    .D(multiplexer_3_out), .en(decoder_1_out2), .clk(clock_1_out), .Q(REG_P_q));  // open: clr
  Register #(.width(16)) REG_B (
    .D(multiplexer_3_out), .en(decoder_1_out3), .clk(clock_1_out), .Q(REG_B_q));  // open: clr
  Adder #(.width(16)) adder_1 (.a(DM_dout), .b(REG_B_q), .out(adder_1_out));  // open: cin, cout
  Subtractor #(.width(16)) subtractor_1 (.a(DM_dout), .b(REG_B_q), .out(subtractor_1_out));  // open: bin, bout
  Comparator #(.width(16)) comparator_1 (
    .a(DM_dout), .b(REG_B_q), .gt(comparator_1_gt), .eq(comparator_1_eq), .lt(comparator_1_lt));
  not not_1 (not_1_out, comparator_1_eq);
  ROM #(.addrWidth(16), .dataWidth(16)) ROM_1 (
    .addr(PC_q),
    .data({ROM_1_data_3[15], ROM_1_data, ROM_1_data_3[11], ROM_1_data_2, ROM_1_data_5, ROM_1_data_4}));
  not not_2 (not_2_out, decoder_1_out4);
  RAM #(.addrWidth(16), .dataWidth(16), .databus("bibus")) DM (
    .addr(REG_P_q), .we(decoder_1_out4), .oe(not_2_out), .clk(clock_1_out), .din(multiplexer_3_out),
    .dout(DM_dout));
  assign Prefix_AND_out = {8{decoder_1_out0[7]}} & {ROM_1_data_5, ROM_1_data_4};  // AND_Gate Prefix_AND, 8 bits wide
  Register Prefix (.D(Prefix_AND_out), .clk(clock_1_out), .Q(Prefix_q));  // open: en, clr
  Multiplexer #(.select(3), .width(16), .enable("false")) multiplexer_2 (
    .in0(adder_1_out), .in1(PC_q), .in2(DM_dout), .in3(REG_B_q), .in4(subtractor_1_out),
    .out(multiplexer_2_out), .sel(ROM_1_data_4));  // open: in5, in6, in7
  Multiplexer #(.width(16), .enable("false")) multiplexer_3 (
    .in0(multiplexer_2_out), .in1({Prefix_q, ROM_1_data_5, ROM_1_data_4}), .out(multiplexer_3_out),
    .sel(ROM_1_data_3[15]));

  // Notes on the sheet:
  //   2
  //   3
  //   1
  //   contents of ROM_1 (hex, n*v repeats v):
  //   8201 8405 8301 404 9103 8100
  //   4
  //   Write Select
  //   Immediate
  //   Read Select
endmodule
